// Logisim project halef_adder.circ as structural Verilog: 1 circuit, main circuit main
module main (
  input  X,
  input  Y,
  output sum,
  output carry
);

  xor xor_1 (sum, X, Y);
  and and_1 (carry, X, Y);
endmodule
