// Logisim project logisim.circ as structural Verilog: 1 circuit, main circuit main
module main (
);

  wire and_1_out, X_out, xor_1_out, Y_out;

  Button X (.out(X_out));
  Button Y (.out(Y_out));
  xor xor_1 (xor_1_out, X_out, Y_out);
  and and_1 (and_1_out, X_out, Y_out);
  Button carry (.out(and_1_out));
  Button sum (.out(xor_1_out));
endmodule
